// Logisim project CPU_CU_SingleCycle.circ as structural Verilog
module Inst_Decoder (
  input  [3:0] Op,
  input  [2:0] Funct,
  output SLL,
  output ROL,
  output SRL,
  output SRA,
  output AND,
  output OR,
  output NOR,
  output XOR,
  output ADD,
  output SUB,
  output SLT,
  output SLTU,
  output JR,
  output ANDI,
  output ORI,
  output LW,
  output SW,
  output ADDI,
  output BEQ,
  output SLTI,
  output BNE,
  output J,
  output Jal,
  output LUI
);

  wire and_1_out, and_2_out, nor_1_out, not_1_out, not_2_out;

  not not_1 (not_1_out, Op[0]);
  nor nor_1 (nor_1_out, Op[3], Op[2], Op[1]);
  Decoder #(.select(3)) decoder_1 (
    .out0(SLL), .out1(ROL), .out2(SRL), .out3(SRA), .out4(AND), .out5(OR), .out6(NOR), .out7(XOR),
    .sel(Funct), .en(and_1_out));
  and and_1 (and_1_out, not_1_out, nor_1_out);
  and and_2 (and_2_out, nor_1_out, Op[0]);
  not not_2 (not_2_out, nor_1_out);
  Decoder #(.select(4)) decoder_2 (
    .out4(ANDI), .out5(ORI), .out6(LW), .out7(SW), .out8(ADDI), .out9(BEQ), .out10(SLTI), .out11(BNE),
    .out12(J), .out13(Jal), .out15(LUI), .sel(Op), .en(not_2_out));  // open: out0, out1, out2, out3, out14
  Decoder #(.select(3)) decoder_3 (
    .out0(ADD), .out1(SUB), .out2(SLT), .out3(SLTU), .out7(JR), .sel(Funct), .en(and_2_out));  // open: out4, out5, out6

  // Notes on the sheet:
  //   ORI: pull=down
  //   ROL: pull=down
  //   SW: pull=down
  //   OR: pull=down
  //   SLTI: pull=down
  //   NOR: pull=down
  //   ADD: pull=down
  //   SRA: pull=down
  //   Funct: pull=down
  //   JR: pull=down
  //   Op: pull=down
  //   SRL: pull=down
  //   AND: pull=down
  //   ANDI: pull=down
  //   SLT: pull=down
  //   ADDI: pull=down
  //   SLL: pull=down
  //   LUI: pull=down
  //   J: pull=down
  //   SUB: pull=down
  //   BNE: pull=down
  //   LW: pull=down
  //   BEQ: pull=down
  //   Jal: pull=down
  //   XOR: pull=down
  //   SLTU: pull=down
  //   is R Format
  //   is not R Format
endmodule

module CS_Gen (
  input  SLL,
  input  ROL,
  input  SRL,
  input  SRA,
  input  AND,
  input  OR,
  input  NOR,
  input  XOR,
  input  ADD,
  input  SUB,
  input  SLT,
  input  SLTU,
  input  JR,
  input  ANDI,
  input  ORI,
  input  LW,
  input  SW,
  input  ADDI,
  input  BEQ,
  input  SLTI,
  input  BNE,
  input  J,
  input  JAL,
  input  LUI,
  input  zero,
  output [3:0] ALUOp,
  output [1:0] PCSrc,
  output ExtOp,
  output MemWr,
  output [1:0] RegDst,
  output MemRd,
  output RegWr,
  output [1:0] WBdata,
  output ALUSrc
);

  wire and_1_out, and_2_out, not_1_out, or_1_out, or_2_out, or_3_out, xor_1_out, xor_2_out;

  xor xor_1 (xor_1_out, ANDI, AND);
  xor xor_2 (xor_2_out, SLTI, SLT);
  or or_1 (or_1_out, OR, ORI);
  not not_1 (not_1_out, zero);
  or or_2 (or_2_out, SUB, BEQ, BNE);
  or or_3 (or_3_out, ADD, ADDI, SW, LW);
  and and_1 (and_1_out, BEQ, zero);
  and and_2 (and_2_out, BNE, not_1_out);
  or or_4 (RegDst[1], JAL, LUI);
  or or_5 (PCSrc[1], JR, J, JAL);
  or or_6 (PCSrc[0], and_1_out, JR, and_2_out);
  nor nor_1 (ExtOp, ANDI, ORI);
  or or_7 (RegDst[0], ANDI, ORI, LW, JAL, BNE, BEQ, SW, SLTI, ADDI);
  Priority_Encoder #(.select(4)) priority_encoder_1 (
    .in0(SLL), .in1(ROL), .in2(SRL), .in3(SRA), .in4(1'b0), .in5(1'b0), .in6(xor_2_out), .in7(SLTU),
    .in8(or_3_out), .in9(or_2_out), .in10(1'b0), .in11(1'b0), .in12(xor_1_out), .in13(or_1_out), .in14(NOR),
    .in15(XOR), .out(ALUOp), .en_in(1'b1));  // open: gs, en_out
  nor nor_2 (RegWr, JR, SW, BEQ, BNE, J);
  or or_8 (WBdata[0], LW, JAL);
  nor nor_3 (ALUSrc, ANDI, ORI, LW, SLTI, SW, ADDI);
  not not_2 (WBdata[1], RegDst[1]);

  assign MemRd = LW;
  assign MemWr = SW;

  // Notes on the sheet:
  //   ExtOp: pull=down
  //   PCSrc: pull=down
  //   SRL: pull=down
  //   J: pull=down
  //   ANDI: pull=down
  //   SLTI: pull=down
  //   BEQ: pull=down
  //   SUB: pull=down
  //   AND: pull=down
  //   NOR: pull=down
  //   OR: pull=down
  //   JAL: pull=down
  //   ADD: pull=down
  //   SLTU: pull=down
  //   ROL: pull=down
  //   ADDI: pull=down
  //   ALUOp: pull=down
  //   LUI: pull=down
  //   LW: pull=down
  //   SLT: pull=down
  //   SRA: pull=down
  //   ORI: pull=down
  //   BNE: pull=down
  //   MemRd: pull=down
  //   SW: pull=down
  //   SLL: pull=down
  //   JR: pull=down
  //   PCSrc[1]
  //   PCSrc[0]
  //   RegDst[0]
  //   WBdata[0]
  //   RegDst[1]
endmodule
