// Logisim project CPU_singleCycle.circ as structural Verilog: 1 circuit, main circuit main
module main (
  input  clock
);

  wire alu_1_zero, main_1_alusrc, main_1_extop, main_1_memrd, main_1_memwr, main_1_regwr;
  wire [1:0] main_1_pcsrc, main_1_regdst, main_1_wbdata;
  wire [2:0] multiplexer_2_out;
  wire [3:0] main_1_aluop, rom_1_data;
  wire [11:0] adder_1_out, multiplexer_1_out, nextpc_1_nextpc, PC_q;
  wire [15:0] alu_1_alu_result, ext_1_result, multiplexer_3_out, multiplexer_4_out, ram_1_data,
       registers_1_busa, registers_1_busb;
  wire [15:4] rom_1_data_2;

  Multiplexer #(.select(2), .width(12), .enable("false")) multiplexer_1 (
    .in0(nextpc_1_nextpc), .in1(adder_1_out), .in2(rom_1_data_2), .in3(registers_1_busa[11:0]),
    .out(multiplexer_1_out), .sel(main_1_pcsrc));
  nextPC nextpc_1 (.PC(PC_q), .NextPC(nextpc_1_nextpc));
  Register #(.width(12)) PC (.D(multiplexer_1_out), .Q(PC_q), .clk(clock));  // open: en, clr
  ROM #(.addrWidth(12), .dataWidth(16)) rom_1 (.addr(PC_q), .data({rom_1_data, rom_1_data_2}));  // open: sel
  Multiplexer #(.select(2), .width(3), .enable("false")) multiplexer_2 (
    .in0(rom_1_data_2[9:7]), .in1(rom_1_data_2[12:10]), .in2(3'b001), .in3(3'b111), .out(multiplexer_2_out),
    .sel(main_1_regdst));
  Ext ext_1 (.ExtOp(main_1_extop), .imm6(rom_1_data_2[9:4]), .result(ext_1_result));
  Adder #(.width(12)) adder_1 (.a(PC_q), .b(ext_1_result[11:0]), .out(adder_1_out));  // open: cin, cout
  registers registers_1 (
    .BusW(multiplexer_4_out), .RegWrite(main_1_regwr), .clk(clock), .RA(rom_1_data_2[15:13]),
    .BusA(registers_1_busa), .BusB(registers_1_busb), .RW(multiplexer_2_out), .RB(rom_1_data_2[12:10]));
  singleCycle_mainControl_main main_1 (
    .Op(rom_1_data), .Funct(rom_1_data_2[6:4]), .ExtOp(main_1_extop), .MemWr(main_1_memwr),
    .RegDst(main_1_regdst), .MemRd(main_1_memrd), .RegWr(main_1_regwr), .WBdata(main_1_wbdata),
    .ALUSrc(main_1_alusrc), .ALUOp(main_1_aluop), .PCSrc(main_1_pcsrc), .Zero(alu_1_zero));
  Multiplexer #(.width(16), .enable("false")) multiplexer_3 (
    .in0(ext_1_result), .in1(registers_1_busb), .out(multiplexer_3_out), .sel(main_1_alusrc));
  ALU alu_1 (
    .A(registers_1_busa), .B(multiplexer_3_out), .ALUOp(main_1_aluop), .ALU_Result(alu_1_alu_result),
    .zero(alu_1_zero));
  RAM #(.addrWidth(12), .dataWidth(16), .bus("separate")) ram_1 (
    .addr(alu_1_alu_result[11:0]), .din(registers_1_busb), .data(ram_1_data), .str(main_1_memwr),
    .clk(clock), .ld(main_1_memrd));  // open: sel, clr
  Multiplexer #(.select(2), .width(16), .enable("false")) multiplexer_4 (
    .in0({rom_1_data_2, 4'b0000}), .in1({4'b0000, nextpc_1_nextpc}), .in2(alu_1_alu_result),
    .in3(ram_1_data), .out(multiplexer_4_out), .sel(main_1_wbdata));

  // Notes on the sheet:
  //   PCSrc
  //   Branch Target Address
  //   Jump Target address
  //   Instruction  Memory
  //   contents of rom_1 (hex, n*v repeats v):
  //   fc78 5084 80fd 1268 12b1 12ba 12a2 734 44d 456 518 462 46b 4e1 7040 7101 6140 9242 14a8 b043 14b0
  //   1938 c020 14a8 1930 1 6*0 5045 d030 42d 9000 4 11*0 5081 50c1 14d8 1691 827f b07d 1e07
  //   Op
  //   Imm6
  //   Rs
  //   Rt
  //   Rd
  //   Funct
  //   RegDst
  //   ExtOp
  //   RegWr
  //   ALUSrc
  //   ALUop
  //   PC + 1
  //   Zero
  //   Data Memory
  //   MemWr
  //   MemRd
  //   Imm12 << 4
  //   WBdata
endmodule
