// Logisim project overflow.circ as structural Verilog
module overflow (
  input  MSB_A,
  input  MSB_B,
  input  MSB_R,
  output Overflow
);

  wire and_1_out, and_2_out, not_1_out, not_2_out, not_3_out;

  not not_1 (not_1_out, MSB_A);
  not not_2 (not_2_out, MSB_B);
  not not_3 (not_3_out, MSB_R);
  and and_1 (and_1_out, not_1_out, not_2_out, MSB_R);
  and and_2 (and_2_out, MSB_A, MSB_B, not_3_out);
  or or_1 (Overflow, and_1_out, and_2_out);
endmodule
