// Logisim project shifter.circ as structural Verilog: 1 circuit, main circuit main
// Shifter
module main (
  input  [3:0] sa,
  input  [15:0] data,
  input  [1:0] slct,
  output [15:0] data_out
);

  wire [15:0] shifter_1_out, shifter_2_out, shifter_3_out, shifter_4_out;

  Shifter #(.width(16)) shifter_1 (.in(data), .\dist (sa), .out(shifter_1_out));
  Shifter #(.width(16), .shift("rl")) shifter_2 (.in(data), .\dist (sa), .out(shifter_2_out));
  Shifter #(.width(16), .shift("lr")) shifter_3 (.in(data), .\dist (sa), .out(shifter_3_out));
  Shifter #(.width(16), .shift("ar")) shifter_4 (.in(data), .\dist (sa), .out(shifter_4_out));
  Multiplexer #(.select(2), .width(16), .enable("false")) multiplexer_1 (
    .in0(shifter_1_out), .in1(shifter_2_out), .in2(shifter_3_out), .in3(shifter_4_out), .out(data_out),
    .sel(slct));
endmodule
