// Logisim project singleCycle_mainControl.circ as structural Verilog: 1 circuit, main circuit main
module main (
  input  [3:0] Op,
  input  [2:0] Funct,
  input  Zero,
  output [1:0] PCSrc,
  output ExtOp,
  output MemWr,
  output [1:0] RegDst,
  output MemRd,
  output RegWr,
  output [1:0] WBdata,
  output ALUSrc,
  output [3:0] ALUOp
);

  wire inst_decoder_1_add, inst_decoder_1_addi, inst_decoder_1_and, inst_decoder_1_andi, inst_decoder_1_beq,
       inst_decoder_1_bne, inst_decoder_1_j, inst_decoder_1_jal, inst_decoder_1_jr, inst_decoder_1_lui,
       inst_decoder_1_lw, inst_decoder_1_nor, inst_decoder_1_or, inst_decoder_1_ori, inst_decoder_1_rol,
       inst_decoder_1_sll, inst_decoder_1_slt, inst_decoder_1_slti, inst_decoder_1_sltu, inst_decoder_1_sra,
       inst_decoder_1_srl, inst_decoder_1_sub, inst_decoder_1_sw, inst_decoder_1_xor;

  Inst_Decoder inst_decoder_1 (
    .Op(Op), .Funct(Funct), .ANDI(inst_decoder_1_andi), .ORI(inst_decoder_1_ori), .LW(inst_decoder_1_lw),
    .SW(inst_decoder_1_sw), .ADDI(inst_decoder_1_addi), .BEQ(inst_decoder_1_beq), .SLTI(inst_decoder_1_slti),
    .BNE(inst_decoder_1_bne), .J(inst_decoder_1_j), .Jal(inst_decoder_1_jal), .LUI(inst_decoder_1_lui),
    .SLL(inst_decoder_1_sll), .ROL(inst_decoder_1_rol), .SRL(inst_decoder_1_srl), .SRA(inst_decoder_1_sra),
    .AND(inst_decoder_1_and), .OR(inst_decoder_1_or), .NOR(inst_decoder_1_nor), .XOR(inst_decoder_1_xor),
    .ADD(inst_decoder_1_add), .SUB(inst_decoder_1_sub), .SLT(inst_decoder_1_slt), .SLTU(inst_decoder_1_sltu),
    .JR(inst_decoder_1_jr));
  CS_Gen cs_gen_1 (
    .SLL(inst_decoder_1_sll), .ROL(inst_decoder_1_rol), .SRL(inst_decoder_1_srl), .SRA(inst_decoder_1_sra),
    .AND(inst_decoder_1_and), .OR(inst_decoder_1_or), .NOR(inst_decoder_1_nor), .XOR(inst_decoder_1_xor),
    .ADD(inst_decoder_1_add), .SUB(inst_decoder_1_sub), .SLT(inst_decoder_1_slt), .SLTU(inst_decoder_1_sltu),
    .JR(inst_decoder_1_jr), .ANDI(inst_decoder_1_andi), .ORI(inst_decoder_1_ori), .LW(inst_decoder_1_lw),
    .SW(inst_decoder_1_sw), .ADDI(inst_decoder_1_addi), .BEQ(inst_decoder_1_beq), .SLTI(inst_decoder_1_slti),
    .BNE(inst_decoder_1_bne), .J(inst_decoder_1_j), .JAL(inst_decoder_1_jal), .LUI(inst_decoder_1_lui),
    .ALUOp(ALUOp), .PCSrc(PCSrc), .ExtOp(ExtOp), .MemWr(MemWr), .RegDst(RegDst), .MemRd(MemRd),
    .RegWr(RegWr), .WBdata(WBdata), .ALUSrc(ALUSrc), .zero(Zero));

  // Notes on the sheet:
  //   ExtOp: pull=down
  //   ALUOp: pull=down
  //   RegWr: pull=down
  //   Funct: pull=down
  //   MemRd: pull=down
  //   Op: pull=down
  //   RegDst: pull=down
  //   PCSrc: pull=down
  //   WBdata: pull=down
endmodule
